# Fritzing sketch MOSFET Board (saved by Fritzing 0.6.5b)
stripboards: 1

parts:
  Power_plug1 = Power plug
  J1 = Screw terminal - 2 pins [package=THT]
  J2 = Screw terminal - 2 pins [package=THT]
  J4 = female pin header, 2 pins [form="♀ (female)"]
  J5 = female pin header, 2 pins [form="♀ (female)"]
  Q1 = 2N7000_FET_N_Channel [part_number=2N7000]
  Q2 = 2N7000_FET_N_Channel [part_number=2N7000]
  Q3 = 2N7000_FET_N_Channel [part_number=2N7000]

nets:
  N1: Power_plug1.GND, Q1.connector2, Q2.connector2, Q3.connector2
  N2: Power_plug1.VCC, J1.pin1
  N3: J1.pin2, Q1.connector1
  N4: J2.pin1, Q2.connector1
  N5: J2.pin2, Q3.connector1
  N6: J4.pin1, Q1.connector0
  N7: J4.pin2, Q2.connector0
  N8: J5.pin1, Q3.connector0
